# Fritzing sketch rc-brake-lights (saved by Fritzing 0.9.2b)
perfboards: 1

parts:
  IC1 = IC, DIP package, 8 pins [chip_label=STC15W104 part_number=STC15W104]
  C1 = Electrolytic Capacitor [capacitance=10µF package="100 mil [THT, electrolytic]"]
  D1 = Rectifier Diode [part_number=1N4148 package="300 mil [THT]"]
  R1 = Resistor [tolerance=±5% resistance=1k package=THT]
  R2 = Resistor [tolerance=±5% resistance=220 package=THT]
  R3 = Resistor [tolerance=±5% resistance=220 package=THT]
  J1 = female pin header, 3 pins [form="♀ (female)"]
  J2 = female pin header, 3 pins [form="♀ (female)"]
  S1 = Momentary Switch [package=ksa_sealed_tac_switch]

nets:
  N1: IC1.pin2, C1.+, D1.cathode
  N2: IC1.pin3, S1.3
  GND: IC1.pin4, C1.-, J1.pin1, J2.pin1, S1.1, S1.2
  N3: IC1.pin5, R3.Pin_0
  N4: IC1.pin6, R2.Pin_0
  N5: IC1.pin7, R1.Pin_1
  N6: D1.anode, J1.pin2
  N7: R1.Pin_0, J1.pin3
  N8: R2.Pin_1, J2.pin3
  N9: R3.Pin_1, J2.pin2

notes:
  Setup button
  Servo input
  GND / Brake / Reverse LED
